// Logisim project Aziz Maulana_200511084.circ as structural Verilog: 4 circuits, main circuit UTS RANGKAIAN DISPLAY NAME 16 SEGMENT
module CIRCUIT_S0_S7 (
  input  T4,
  input  T3,
  input  T2,
  input  T1,
  input  T0,
  output S0,
  output S1,
  output S2,
  output S3,
  output S4,
  output S5,
  output S6,
  output S7
);

  wire and_1_out, and_2_out, and_3_out, and_4_out, and_5_out, and_6_out, and_7_out, and_8_out, and_10_out,
       and_11_out, and_12_out, and_13_out, and_14_out, and_15_out, and_16_out, and_17_out, not_1_out,
       not_2_out, not_3_out, not_4_out, not_5_out, not_6_out, not_7_out, not_8_out, not_9_out, not_10_out,
       not_11_out, not_12_out, not_13_out, not_14_out, not_15_out, not_16_out, not_17_out, not_18_out,
       not_19_out, not_20_out, not_21_out, not_22_out, not_23_out, not_24_out, not_25_out, not_26_out,
       not_27_out, not_28_out, not_29_out, not_30_out, not_31_out;

  not not_1 (not_1_out, T3);
  not not_2 (not_2_out, T2);
  not not_3 (not_3_out, T3);
  not not_4 (not_4_out, T3);
  not not_5 (not_5_out, T1);
  not not_6 (not_6_out, T0);
  not not_7 (not_7_out, T2);
  not not_8 (not_8_out, T1);
  not not_9 (not_9_out, T0);
  not not_10 (not_10_out, T3);
  not not_11 (not_11_out, T2);
  not not_12 (not_12_out, T1);
  not not_13 (not_13_out, T3);
  not not_14 (not_14_out, T2);
  not not_15 (not_15_out, T0);
  not not_16 (not_16_out, T1);
  not not_17 (not_17_out, T3);
  not not_18 (not_18_out, T0);
  not not_19 (not_19_out, T3);
  not not_20 (not_20_out, T2);
  not not_21 (not_21_out, T3);
  not not_22 (not_22_out, T3);
  not not_23 (not_23_out, T0);
  not not_24 (not_24_out, T3);
  not not_25 (not_25_out, T0);
  not not_26 (not_26_out, T2);
  not not_27 (not_27_out, T1);
  not not_28 (not_28_out, T2);
  not not_29 (not_29_out, T0);
  not not_30 (not_30_out, T3);
  not not_31 (not_31_out, T1);
  and and_1 (and_1_out, T4, not_1_out, not_2_out, T0);
  and and_2 (and_2_out, T4, not_3_out, T1, T0);
  and and_3 (and_3_out, T4, not_4_out, T2, not_5_out, not_6_out);
  and and_4 (and_4_out, T4, T3, not_7_out, not_8_out, not_9_out);
  and and_5 (and_5_out, T4, not_10_out, not_11_out, not_12_out, T0);
  and and_6 (and_6_out, T4, not_13_out, T2, T1, T0);
  and and_7 (and_7_out, T4, T3, not_14_out, T1, not_15_out);
  and and_8 (and_8_out, T4, T3, T2, not_16_out);
  and and_9 (S4, T4, not_17_out, T2, T1, not_18_out);
  and and_10 (and_10_out, T4, not_19_out, not_20_out, T0);
  and and_11 (and_11_out, T4, not_21_out, T1, T0);
  and and_12 (and_12_out, T4, not_22_out, T1, not_23_out);
  and and_13 (and_13_out, T4, not_24_out, T2, not_25_out);
  and and_14 (and_14_out, T4, T3, not_26_out, not_27_out);
  and and_15 (and_15_out, T4, not_28_out, T1, not_29_out);
  and and_16 (and_16_out, T4, not_30_out, T2, T1, T0);
  and and_17 (and_17_out, T4, T3, not_31_out);
  or or_1 (S1, and_1_out, and_2_out);
  or or_2 (S2, and_3_out, and_4_out);
  or or_3 (S3, and_5_out, and_6_out, and_7_out, and_8_out);
  or or_4 (S5, and_10_out, and_11_out);
  or or_5 (S6, and_12_out, and_13_out, and_14_out);
  or or_6 (S7, and_15_out, and_16_out, and_17_out);

  assign S0 = 1'b0;
endmodule

module CIRCUIT_S8_SF (
  input  T4,
  input  T3,
  input  T2,
  input  T1,
  input  T0,
  output S8,
  output S9,
  output SA,
  output SB,
  output SC,
  output SD,
  output SE,
  output SF
);

  wire and_1_out, and_2_out, and_3_out, and_4_out, and_5_out, and_6_out, and_7_out, and_8_out, and_9_out,
       and_10_out, and_11_out, and_12_out, and_13_out, and_14_out, and_15_out, and_16_out, and_17_out,
       and_18_out, and_19_out, and_20_out, and_21_out, and_22_out, and_23_out, and_24_out, and_25_out,
       and_26_out, not_1_out, not_2_out, not_3_out, not_4_out, not_5_out, not_6_out, not_7_out, not_8_out,
       not_9_out, not_10_out, not_11_out, not_12_out, not_13_out, not_14_out, not_15_out, not_16_out,
       not_17_out, not_18_out, not_19_out, not_20_out, not_21_out, not_22_out, not_23_out, not_24_out,
       not_25_out, not_26_out, not_27_out, not_28_out, not_29_out, not_30_out, not_31_out, not_32_out,
       not_33_out, not_34_out, not_35_out, not_36_out, not_37_out, not_38_out, not_39_out, not_40_out,
       not_41_out, not_42_out, not_43_out, not_44_out, not_45_out;

  not not_1 (not_1_out, T3);
  not not_2 (not_2_out, T1);
  not not_3 (not_3_out, T1);
  not not_4 (not_4_out, T0);
  not not_5 (not_5_out, T2);
  not not_6 (not_6_out, T3);
  not not_7 (not_7_out, T1);
  not not_8 (not_8_out, T1);
  not not_9 (not_9_out, T0);
  not not_10 (not_10_out, T2);
  not not_11 (not_11_out, T3);
  not not_12 (not_12_out, T2);
  not not_13 (not_13_out, T1);
  not not_14 (not_14_out, T3);
  not not_15 (not_15_out, T0);
  not not_16 (not_16_out, T2);
  not not_17 (not_17_out, T1);
  not not_18 (not_18_out, T0);
  not not_19 (not_19_out, T3);
  not not_20 (not_20_out, T2);
  not not_21 (not_21_out, T1);
  not not_22 (not_22_out, T3);
  not not_23 (not_23_out, T0);
  not not_24 (not_24_out, T2);
  not not_25 (not_25_out, T1);
  not not_26 (not_26_out, T3);
  not not_27 (not_27_out, T2);
  not not_28 (not_28_out, T1);
  not not_29 (not_29_out, T1);
  not not_30 (not_30_out, T0);
  not not_31 (not_31_out, T2);
  not not_32 (not_32_out, T3);
  not not_33 (not_33_out, T2);
  not not_34 (not_34_out, T0);
  not not_35 (not_35_out, T1);
  not not_36 (not_36_out, T0);
  not not_37 (not_37_out, T2);
  not not_38 (not_38_out, T3);
  not not_39 (not_39_out, T0);
  not not_40 (not_40_out, T1);
  not not_41 (not_41_out, T2);
  not not_42 (not_42_out, T3);
  not not_43 (not_43_out, T0);
  not not_44 (not_44_out, T1);
  not not_45 (not_45_out, T2);
  and and_1 (and_1_out, T4, not_1_out, T2, not_2_out);
  and and_2 (and_2_out, T4, T2, not_3_out, not_4_out);
  and and_3 (and_3_out, T4, T3, not_5_out, T1, T0);
  and and_4 (and_4_out, T4, not_6_out, T2, not_7_out);
  and and_5 (and_5_out, T4, T2, not_8_out, not_9_out);
  and and_6 (and_6_out, T4, T3, not_10_out, T1, T0);
  and and_7 (and_7_out, T4, not_11_out, not_12_out, not_13_out, T0);
  and and_8 (and_8_out, T4, not_14_out, T2, T1, not_15_out);
  and and_9 (and_9_out, T4, T3, not_16_out, T1, T0);
  and and_10 (and_10_out, T4, T3, T2, not_17_out, not_18_out);
  and and_11 (and_11_out, T4, not_19_out, not_20_out, not_21_out, T0);
  and and_12 (and_12_out, T4, not_22_out, T2, T1, not_23_out);
  and and_13 (and_13_out, T4, T3, not_24_out, T1, T0);
  and and_14 (and_14_out, T4, T3, T2, not_25_out);
  and and_15 (and_15_out, T4, not_26_out, not_27_out, not_28_out, T0);
  and and_16 (and_16_out, T4, T2, not_29_out, not_30_out);
  and and_17 (and_17_out, T4, T3, not_31_out, T1, T0);
  and and_18 (and_18_out, T4, not_32_out, not_33_out, T1, not_34_out);
  and and_19 (and_19_out, T4, T2, not_35_out, not_36_out);
  and and_20 (and_20_out, T4, T3, not_37_out, T1, T0);
  and and_21 (and_21_out, T4, not_38_out, T2, T1, not_39_out);
  and and_22 (and_22_out, T4, T3, not_40_out);
  and and_23 (and_23_out, T4, T3, not_41_out, T0);
  and and_24 (and_24_out, T4, not_42_out, T2, T1, not_43_out);
  and and_25 (and_25_out, T4, T3, not_44_out);
  and and_26 (and_26_out, T4, T3, not_45_out, T0);
  or or_1 (S8, and_1_out, and_2_out, and_3_out);
  or or_2 (S9, and_4_out, and_5_out, and_6_out);
  or or_3 (SA, and_7_out, and_8_out, and_9_out, and_10_out);
  or or_4 (SB, and_11_out, and_12_out, and_13_out, and_14_out);
  or or_5 (SC, and_15_out, and_16_out, and_17_out);
  or or_6 (SD, and_18_out, and_19_out, and_20_out);
  or or_7 (SE, and_21_out, and_22_out, and_23_out);
  or or_8 (SF, and_24_out, and_25_out, and_26_out);
endmodule

// 16 SEGMENT
module CIRCUIT_16_SEGMENT (
  input  in_1,
  input  in_2,
  input  in_3,
  input  in_4,
  input  in_5,
  output out_6,
  output out_7,
  output out_8,
  output out_9,
  output out_10,
  output out_11,
  output out_12,
  output out_13,
  output out_14,
  output out_15,
  output out_16,
  output out_17,
  output out_18,
  output out_19,
  output out_20,
  output out_21
);

  CIRCUIT_S0_S7 circuit_s0_s7_1 (
    .T4(in_1), .T3(in_2), .T2(in_3), .T1(in_4), .T0(in_5), .S0(out_6), .S1(out_7), .S2(out_8), .S3(out_9),
    .S4(out_10), .S5(out_11), .S6(out_12), .S7(out_13));
  CIRCUIT_S8_SF circuit_s8_sf_1 (
    .T4(in_1), .T3(in_2), .T2(in_3), .T1(in_4), .T0(in_5), .S8(out_14), .S9(out_15), .SA(out_16),
    .SB(out_17), .SC(out_18), .SD(out_19), .SE(out_20), .SF(out_21));
endmodule

module UTS_RANGKAIAN_DISPLAY_NAME_16_SEGMENT (
  input  T4,
  input  T3,
  input  T2,
  input  T1,
  input  T0
);

  wire [15:0] circuit_16_segment_1_out_21;

  CIRCUIT_16_SEGMENT circuit_16_segment_1 (
    .in_1(T4), .in_2(T3), .in_3(T2), .in_4(T1), .in_5(T0), .out_6(circuit_16_segment_1_out_21[15]),
    .out_7(circuit_16_segment_1_out_21[14]), .out_8(circuit_16_segment_1_out_21[13]),
    .out_9(circuit_16_segment_1_out_21[12]), .out_10(circuit_16_segment_1_out_21[11]),
    .out_11(circuit_16_segment_1_out_21[10]), .out_12(circuit_16_segment_1_out_21[9]),
    .out_13(circuit_16_segment_1_out_21[8]), .out_14(circuit_16_segment_1_out_21[7]),
    .out_15(circuit_16_segment_1_out_21[6]), .out_16(circuit_16_segment_1_out_21[5]),
    .out_17(circuit_16_segment_1_out_21[4]), .out_18(circuit_16_segment_1_out_21[3]),
    .out_19(circuit_16_segment_1_out_21[2]), .out_20(circuit_16_segment_1_out_21[1]),
    .out_21(circuit_16_segment_1_out_21[0]));
  LED led_1 (.in(circuit_16_segment_1_out_21[4]));
  LED led_2 (.in(circuit_16_segment_1_out_21[11]));
  LED led_3 (.in(circuit_16_segment_1_out_21[4]));
  LED led_4 (.in(circuit_16_segment_1_out_21[4]));
  LED led_5 (.in(circuit_16_segment_1_out_21[4]));
  LED led_6 (.in(circuit_16_segment_1_out_21[4]));
  LED led_7 (.in(circuit_16_segment_1_out_21[12]));
  LED led_8 (.in(circuit_16_segment_1_out_21[5]));
  LED led_9 (.in(circuit_16_segment_1_out_21[5]));
  LED led_10 (.in(circuit_16_segment_1_out_21[5]));
  LED led_11 (.in(circuit_16_segment_1_out_21[5]));
  LED led_12 (.in(circuit_16_segment_1_out_21[5]));
  LED led_13 (.in(circuit_16_segment_1_out_21[3]));
  LED led_14 (.in(circuit_16_segment_1_out_21[3]));
  LED led_15 (.in(circuit_16_segment_1_out_21[3]));
  LED led_16 (.in(circuit_16_segment_1_out_21[3]));
  LED led_17 (.in(circuit_16_segment_1_out_21[11]));
  LED led_18 (.in(circuit_16_segment_1_out_21[11]));
  LED led_19 (.in(circuit_16_segment_1_out_21[11]));
  LED led_20 (.in(circuit_16_segment_1_out_21[11]));
  LED led_21 (.in(circuit_16_segment_1_out_21[12]));
  LED led_22 (.in(circuit_16_segment_1_out_21[12]));
  LED led_23 (.in(circuit_16_segment_1_out_21[12]));
  LED led_24 (.in(circuit_16_segment_1_out_21[12]));
  LED led_25 (.in(circuit_16_segment_1_out_21[13]));
  LED led_26 (.in(circuit_16_segment_1_out_21[13]));
  LED led_27 (.in(circuit_16_segment_1_out_21[13]));
  LED led_28 (.in(circuit_16_segment_1_out_21[13]));
  LED led_29 (.in(circuit_16_segment_1_out_21[6]));
  LED led_30 (.in(circuit_16_segment_1_out_21[6]));
  LED led_31 (.in(circuit_16_segment_1_out_21[6]));
  LED led_32 (.in(circuit_16_segment_1_out_21[6]));
  LED led_33 (.in(circuit_16_segment_1_out_21[2]));
  LED led_34 (.in(circuit_16_segment_1_out_21[2]));
  LED led_35 (.in(circuit_16_segment_1_out_21[10]));
  LED led_36 (.in(circuit_16_segment_1_out_21[10]));
  LED led_37 (.in(circuit_16_segment_1_out_21[10]));
  LED led_38 (.in(circuit_16_segment_1_out_21[10]));
  LED led_39 (.in(circuit_16_segment_1_out_21[9]));
  LED led_40 (.in(circuit_16_segment_1_out_21[10]));
  LED led_41 (.in(circuit_16_segment_1_out_21[9]));
  LED led_42 (.in(circuit_16_segment_1_out_21[8]));
  LED led_43 (.in(circuit_16_segment_1_out_21[8]));
  LED led_44 (.in(circuit_16_segment_1_out_21[15]));
  LED led_45 (.in(circuit_16_segment_1_out_21[14]));
  LED led_46 (.in(circuit_16_segment_1_out_21[13]));
  LED led_47 (.in(circuit_16_segment_1_out_21[14]));
  LED led_48 (.in(circuit_16_segment_1_out_21[15]));
  LED led_49 (.in(circuit_16_segment_1_out_21[14]));
  LED led_50 (.in(circuit_16_segment_1_out_21[14]));
  LED led_51 (.in(circuit_16_segment_1_out_21[14]));
  LED led_52 (.in(circuit_16_segment_1_out_21[7]));
  LED led_53 (.in(circuit_16_segment_1_out_21[7]));
  LED led_54 (.in(circuit_16_segment_1_out_21[2]));
  LED led_55 (.in(circuit_16_segment_1_out_21[2]));
  LED led_56 (.in(circuit_16_segment_1_out_21[1]));
  LED led_57 (.in(circuit_16_segment_1_out_21[9]));
  LED led_58 (.in(circuit_16_segment_1_out_21[1]));
  LED led_59 (.in(circuit_16_segment_1_out_21[9]));
  LED led_60 (.in(circuit_16_segment_1_out_21[1]));
  LED led_61 (.in(circuit_16_segment_1_out_21[9]));
  LED led_62 (.in(circuit_16_segment_1_out_21[1]));
  LED led_63 (.in(circuit_16_segment_1_out_21[1]));
  LED led_64 (.in(circuit_16_segment_1_out_21[8]));
  LED led_65 (.in(circuit_16_segment_1_out_21[8]));
  LED led_66 (.in(circuit_16_segment_1_out_21[8]));
  LED led_67 (.in(circuit_16_segment_1_out_21[0]));
  LED led_68 (.in(circuit_16_segment_1_out_21[0]));
  LED led_69 (.in(circuit_16_segment_1_out_21[0]));
  LED led_70 (.in(circuit_16_segment_1_out_21[15]));
  LED led_71 (.in(circuit_16_segment_1_out_21[15]));
  LED led_72 (.in(circuit_16_segment_1_out_21[0]));
  LED led_73 (.in(circuit_16_segment_1_out_21[0]));
  LED led_74 (.in(circuit_16_segment_1_out_21[15]));
  LED led_75 (.in(circuit_16_segment_1_out_21[7]));
  LED led_76 (.in(circuit_16_segment_1_out_21[7]));

  // Notes on the sheet:
  //   AZIZ_M+A4-084
  //   A = 1 0 0 0 1 
  //   Z = 1 0 0 1 0
  //   I = 1 0 0 1 1
  //   Z = 1 0 1 0 0
  //   _ = 1 0 1 0 1
  //   M = 1 0 1 1 0
  //   += 1 0 1 1 1
  //   A = 1 1 0 0 0
  //   4 = 1 1 0 0 1
  //   - = 1 1 0 1 0
  //   0 = 1 1 0 1 1
  //   8 = 1 1 1 0 0
  //   4 = 1 1 1 0 1
  //   Perancangan Rangkaian Logika Kombinatorial
  //   "Display Alfabet & Number"
  //   SB
  //   SA
  //   SC
  //   4
  //   3
  //   2
  //   9
  //   SD
  //   5
  //   6
  //   0
  //   1
  //   8
  //   Nama : Aziz Maulana
  //   Kelas : A4
  //   Nim : 200511084
  //   Semester : 2
  //   SE
  //   7
  //   SF
  //   Mata Kuliah : Sistem Digital
  //   Fakultas/Prodi : Teknik Informatika
endmodule
